// Logisim project Project1Given.circ as structural Verilog: 4 circuits, main circuit main
module main (
  input  in_1,
  input  in_2,
  input  in_3,
  input  in_4,
  input  Five,
  output N,
  output E,
  output [3:0] out_8
);

  wire fiveseven_1_a, fiveseven_1_b, fiveseven_1_c, fiveseven_1_d, fiveseven_1_e, fiveseven_1_f,
       fiveseven_1_g;

  Compare compare_1 (.X0(1'b1), .Y0(1'b1), .X1(1'b1), .Y1(1'b1), .X2(1'b0), .Y2(1'b0), .N(N), .E(E));
  Gray gray_1 (.B0(1'b1), .B1(1'b0), .B2(1'b1), .B3(1'b1), .G0(out_8[0]), .G2(out_8[1]), .G3(out_8[2]), .G1(out_8[3]));
  FiveSeven fiveseven_1 (
    .V(in_1), .W(in_2), .X(in_3), .Y(in_4), .Z(Five), .A(fiveseven_1_a), .B(fiveseven_1_b),
    .C(fiveseven_1_c), .D(fiveseven_1_d), .E(fiveseven_1_e), .F(fiveseven_1_f), .G(fiveseven_1_g));
  _7_Segment_Display u_7_segment_display_1 (
    .g(fiveseven_1_g), .f(fiveseven_1_f), .a(fiveseven_1_a), .b(fiveseven_1_b), .e(fiveseven_1_e),
    .d(fiveseven_1_d), .c(fiveseven_1_c));  // open: dp
endmodule

module Compare (
  input  X0,
  input  Y0,
  input  X1,
  input  Y1,
  input  X2,
  input  Y2,
  output N,
  output E
);

  wire c1_out, c2_out, c3_out, not_1_out, not_2_out, not_3_out, xnor_1_out, xnor_2_out, xnor_3_out;

  xnor xnor_1 (xnor_1_out, X0, Y0);
  xnor xnor_2 (xnor_2_out, X1, Y1);
  xnor xnor_3 (xnor_3_out, X2, Y2);
  and and_1 (E, xnor_1_out, xnor_2_out, xnor_3_out);
  not not_1 (not_1_out, X2);
  and c1 (c1_out, not_1_out, Y2);
  not not_2 (not_2_out, X1);
  and c2 (c2_out, not_2_out, Y1, xnor_3_out);
  not not_3 (not_3_out, X0);
  and c3 (c3_out, not_3_out, Y0, xnor_3_out, xnor_2_out);
  or or_1 (N, c3_out, c2_out, c1_out);
endmodule

module Gray (
  input  B0,
  input  B1,
  input  B2,
  input  B3,
  output G0,
  output G2,
  output G3,
  output G1
);

  wire and_1_out, and_2_out, not_1_out, not_2_out, not_3_out, or_1_out;

  or or_1 (or_1_out, B0, B1);
  not not_1 (not_1_out, B1);
  not not_2 (not_2_out, B0);
  and and_1 (and_1_out, not_1_out, not_2_out, not_3_out);
  not not_3 (not_3_out, B2);
  and and_2 (and_2_out, or_1_out, B2);
  not not_4 (G0, B1);
  or or_2 (G1, and_2_out, and_1_out);
endmodule

module FiveSeven (
  input  V,
  input  W,
  input  X,
  input  Y,
  input  Z,
  output A,
  output B,
  output C,
  output D,
  output E,
  output F,
  output G
);
endmodule
